// Logisim project Lab10Part1-rlb97.circ as structural Verilog: 1 circuit, main circuit main
module main (
  input  WriteEnable,
  input  [1:0] ReadRegister1,
  input  [1:0] ReadRegister2,
  input  [1:0] WriteRegister,
  input  [15:0] WriteData,
  input  Clock,
  output [15:0] ReadData1,
  output [15:0] ReadData2
);

  wire [15:0] _00_q, _01_q, _10_q, _11_q, demultiplexer_1_out0, demultiplexer_1_out1, demultiplexer_1_out2,
       demultiplexer_1_out3, multiplexer_1_out, multiplexer_2_out, multiplexer_3_out;

  Multiplexer #(.width(16)) multiplexer_1 (
    .in0({16{1'b0}}), .in1(WriteData), .out(multiplexer_1_out), .sel(WriteEnable));  // open: en
  Demultiplexer #(.select(2), .width(16)) demultiplexer_1 (
    .out0(demultiplexer_1_out0), .out1(demultiplexer_1_out1), .out2(demultiplexer_1_out2),
    .out3(demultiplexer_1_out3), .in(multiplexer_1_out), .sel(WriteRegister));  // open: en
  Register #(.width(16)) _01 (.D(demultiplexer_1_out1), .Q(_01_q), .clk(Clock), .clr(1'b0));  // open: en
  Register #(.width(16)) _10 (.D(demultiplexer_1_out2), .Q(_10_q), .clk(Clock), .clr(1'b0));  // open: en
  Register #(.width(16)) _11 (.D(demultiplexer_1_out3), .Q(_11_q), .clk(Clock), .clr(1'b0));  // open: en
  Register #(.width(16)) _00 (.D(demultiplexer_1_out0), .Q(_00_q), .clk(Clock), .clr(1'b0));  // open: en
  Multiplexer #(.select(2), .width(16)) multiplexer_2 (
    .in0(_00_q), .in1(_01_q), .in2(_10_q), .in3(_11_q), .out(multiplexer_2_out), .sel(ReadRegister1));  // open: en
  Multiplexer #(.select(2), .width(16)) multiplexer_3 (
    .in0(_00_q), .in1(_01_q), .in2(_10_q), .in3(_11_q), .out(multiplexer_3_out), .sel(ReadRegister2));  // open: en
  Multiplexer #(.width(16)) multiplexer_4 (
    .in0(multiplexer_2_out), .in1(ReadData1), .out(ReadData1), .sel(WriteEnable));  // open: en
  Multiplexer #(.width(16)) multiplexer_5 (
    .in0(multiplexer_3_out), .in1(ReadData2), .out(ReadData2), .sel(WriteEnable));  // open: en
endmodule
