// Logisim project Lab09Part1-rlb97.circ as structural Verilog: 1 circuit, main circuit main
module main (
  input  A1,
  input  A2,
  input  B1,
  input  B2,
  output OUTPUT
);

  wire _0001_out, _0010_out, _0100_out, _0111_out, _1000_out, _1011_out, _1101_out, _1110_out, A00_out,
       A01_out, A10_out, A11_out, B00_out, B01_out, B10_out, B11_out, not_1_out, not_2_out, not_3_out,
       not_4_out, OR1_out, OR2_out, OR3_out, OR4_out, OR5_out, OR6_out;

  not not_1 (not_1_out, A1);
  not not_2 (not_2_out, A2);
  not not_3 (not_3_out, B1);
  not not_4 (not_4_out, B2);
  and A00 (A00_out, not_2_out, not_1_out);
  and A01 (A01_out, not_1_out, A2);
  and A11 (A11_out, A1, A2);
  and A10 (A10_out, A1, not_2_out);
  and B00 (B00_out, not_4_out, not_3_out);
  and B01 (B01_out, not_3_out, B2);
  and B11 (B11_out, B1, B2);
  and B10 (B10_out, B1, not_4_out);
  and _1110 (_1110_out, A11_out, B10_out);
  and _1101 (_1101_out, A11_out, B01_out);
  and _0100 (_0100_out, A01_out, B00_out);
  and _0001 (_0001_out, A00_out, B01_out);
  and _0111 (_0111_out, A01_out, B11_out);
  and _0010 (_0010_out, A00_out, B10_out);
  and _1000 (_1000_out, A10_out, B00_out);
  and _1011 (_1011_out, A10_out, B11_out);
  or OR1 (OR1_out, _1110_out, _1101_out);
  or OR2 (OR2_out, _1000_out, _0100_out);
  or OR3 (OR3_out, _0001_out, _1011_out);
  or OR4 (OR4_out, _0111_out, _0010_out);
  or OR5 (OR5_out, OR1_out, OR2_out);
  or OR6 (OR6_out, OR3_out, OR4_out);
  or OR7 (OUTPUT, OR5_out, OR6_out);
endmodule
