// Logisim project Project2-rlby97.circ as structural Verilog: 14 circuits, main circuit main
module main (
);

  wire ADDI_bez, ADDI_bne, ADDI_CONTROL_addi, BEQ_out, BNE_out, Branch_Control_branchequal,
       Branch_Control_brancnotequal, Branch_out, clock_1_out, HALT, MemRead, MemWrite, not_1_out, or_1_out,
       or_2_out, PUT, signalcontrol_1_alusrc, signalcontrol_1_j, signalcontrol_1_jal, signalcontrol_1_jr,
       signalcontrol_1_memtoreg, signalcontrol_1_regwrite;
  wire [1:0] ALUOP;
  wire [2:0] ALU_CONTROL_alucontrol3;
  wire [3:0] Display_Register_q_2, rom_1_data_2;
  wire [7:0] adder_1_out, bit_extender_3_out, multiplexer_3_out, multiplexer_6_out, multiplexer_7_out, PC_q;
  wire [11:0] rom_1_data;
  wire [15:0] adder_2_out, ADDI_result, ALU_aluresult, bit_extender_1_out, bit_extender_2_out,
       Display_Register_q, multiplexer_1_out, multiplexer_2_out, multiplexer_4_out, multiplexer_5_out,
       multiplexer_8_out, ram_1_data, Register_Memory_regdata1, Register_Memory_regdata2;

  Clock clock_1 (.out(clock_1_out));
  not not_1 (not_1_out, HALT);
  Register PC (.D(multiplexer_7_out), .en(not_1_out), .Q(PC_q), .clk(clock_1_out));  // open: clr
  Adder adder_1 (.a(PC_q), .b(8'h1), .out(adder_1_out));  // open: cin, cout
  SignalControl signalcontrol_1 (
    .OP1(rom_1_data_2[3]), .OP2(rom_1_data_2[2]), .OP3(rom_1_data_2[1]), .OP4(rom_1_data_2[0]),
    .FUNCT(rom_1_data[0]), .ALUSRC(signalcontrol_1_alusrc), .ALUOP1(ALUOP[0]), .ALUOP2(ALUOP[1]),
    .RegWrite(signalcontrol_1_regwrite), .J(signalcontrol_1_j), .JR(signalcontrol_1_jr),
    .JAL(signalcontrol_1_jal), .MemRead(MemRead), .MemWrite(MemWrite), .MemToReg(signalcontrol_1_memtoreg),
    .PUT(PUT), .HALT(HALT));
  BranchControl Branch_Control (
    .OP1(rom_1_data_2[3]), .OP2(rom_1_data_2[2]), .OP3(rom_1_data_2[1]), .OP4(rom_1_data_2[0]),
    .BranchEqual(Branch_Control_branchequal), .BrancNotEqual(Branch_Control_brancnotequal));
  assign bit_extender_1_out = {{8{1'b0}}, PC_q};  // Bit_Extender bit_extender_1
  ADDI_CONTROL ADDI_CONTROL (
    .OP1(rom_1_data_2[3]), .OP2(rom_1_data_2[2]), .OP3(rom_1_data_2[1]), .OP4(rom_1_data_2[0]),
    .FUNCT(rom_1_data[0]), .ADDI(ADDI_CONTROL_addi));
  ROM #(.dataWidth(16)) rom_1 (.addr(PC_q), .data({rom_1_data_2, rom_1_data}), .sel(1'b1));
  Adder #(.width(16)) adder_2 (.a(bit_extender_1_out), .b(16'h1), .out(adder_2_out));  // open: cin, cout
  Multiplexer #(.width(16), .enable("false")) multiplexer_1 (
    .in0(multiplexer_8_out), .in1(adder_2_out), .out(multiplexer_1_out), .sel(signalcontrol_1_jal));
  Register_Memory Register_Memory (
    .ReadReg1(rom_1_data[11:9]), .ReadReg2(rom_1_data[8:6]), .WriteReg(rom_1_data[11:9]),
    .WriteData(multiplexer_1_out), .WriteEnable(signalcontrol_1_regwrite), .Clock(clock_1_out),
    .RegData1(Register_Memory_regdata1), .RegData2(Register_Memory_regdata2));
  assign bit_extender_2_out = {{8{1'b0}}, rom_1_data[8:1]};  // Bit_Extender bit_extender_2
  ADDI ADDI (
    .Register(Register_Memory_regdata1), .Immediate(rom_1_data[8:1]), .Result(ADDI_result), .BNE(ADDI_bne),
    .BEZ(ADDI_bez));
  Multiplexer #(.width(16), .enable("false")) multiplexer_2 (
    .in0(Register_Memory_regdata2), .in1(bit_extender_2_out), .out(multiplexer_2_out),
    .sel(signalcontrol_1_alusrc));
  ALU ALU (
    .Input_A(Register_Memory_regdata1), .Input_B(multiplexer_2_out), .SHAMT(rom_1_data[4:1]),
    .ALUControl(ALU_CONTROL_alucontrol3), .ALUResult(ALU_aluresult));
  ALU_CONTROL ALU_CONTROL (
    .ALUOP1(ALUOP[0]), .ALUOP2(ALUOP[1]), .FUNCT(rom_1_data[0]), .ALUCONTROL1(ALU_CONTROL_alucontrol3[2]),
    .ALUCONTROL2(ALU_CONTROL_alucontrol3[1]), .ALUCONTROL3(ALU_CONTROL_alucontrol3[0]));
  Multiplexer #(.width(8), .enable("false")) multiplexer_3 (
    .in0(adder_1_out), .in1(rom_1_data[8:1]), .out(multiplexer_3_out), .sel(Branch_out));
  or Branch (Branch_out, BEQ_out, BNE_out);
  and BEQ (BEQ_out, Branch_Control_branchequal, ADDI_bez);
  and BNE (BNE_out, Branch_Control_brancnotequal, ADDI_bne);
  Multiplexer #(.width(16), .enable("false")) multiplexer_4 (
    .in0(ALU_aluresult), .in1(ADDI_result), .out(multiplexer_4_out), .sel(ADDI_CONTROL_addi));
  Multiplexer #(.width(16), .enable("false")) multiplexer_5 (
    .in0(multiplexer_4_out), .in1(Register_Memory_regdata1), .out(multiplexer_5_out), .sel(or_1_out));
  or or_1 (or_1_out, MemRead, MemWrite);
  or or_2 (or_2_out, MemWrite, MemRead);
  Multiplexer #(.width(8), .enable("false")) multiplexer_6 (
    .in0(multiplexer_3_out), .in1(rom_1_data[8:1]), .out(multiplexer_6_out), .sel(signalcontrol_1_j));
  Bit_Extender #(.in_width(16), .out_width(8)) bit_extender_3 (.in(Register_Memory_regdata1), .out(bit_extender_3_out));
  Multiplexer #(.width(8), .disabled(0), .enable("false")) multiplexer_7 (
    .in0(multiplexer_6_out), .in1(bit_extender_3_out), .out(multiplexer_7_out), .sel(signalcontrol_1_jr));
  RAM #(.addrWidth(16), .dataWidth(16), .bus("separate")) ram_1 (
    .addr(Register_Memory_regdata2), .din(multiplexer_5_out), .data(ram_1_data), .str(MemWrite),
    .sel(or_2_out), .clk(clock_1_out), .ld(MemRead));  // open: clr
  Register #(.width(16)) Display_Register (
    .D(Register_Memory_regdata1), .en(PUT),
    .Q({Display_Register_q[15:8], Display_Register_q_2, Display_Register_q[3:0]}), .clk(clock_1_out));  // open: clr
  Multiplexer #(.width(16), .enable("false")) multiplexer_8 (
    .in0(multiplexer_5_out), .in1(ram_1_data), .out(multiplexer_8_out), .sel(signalcontrol_1_memtoreg));
  LED Halt_LED (.in(HALT));
  Hex_Digit_Display hex_digit_display_1 (.value(Display_Register_q[11:8]));  // open: dp
  Hex_Digit_Display hex_digit_display_2 (.value(Display_Register_q[15:12]));  // open: dp
  Hex_Digit_Display hex_digit_display_3 (.value(Display_Register_q[3:0]));  // open: dp
  Hex_Digit_Display hex_digit_display_4 (.value(Display_Register_q_2));  // open: dp

  // Notes on the sheet:
  //   PC+1
  //   Randyll Bearer
  //   rlb97@pitt.edu
  //   Instruction Memory
  //   contents of rom_1 (hex, n*v repeats v):
  //   2402 280a 7501 7f00 e00 2e02 7f01 7d00 c00 2802 2c02 7d01 2802 2c02 7d01 260c 7ec0 e00 2602 7ec0 e00
  //   f000
  //   JAL/Normal
  //   Jump
  //   Immediate
  //   Branch/PC+1
  //   Jump/Whatever
  //   Data Memory
  //   JR/Whatever
endmodule

module Register_Memory (
  input  WriteEnable,
  input  [2:0] ReadReg1,
  input  [2:0] ReadReg2,
  input  [2:0] WriteReg,
  input  [15:0] WriteData,
  input  Clock,
  output [15:0] RegData1,
  output [15:0] RegData2
);

  wire demultiplexer_1_out0, demultiplexer_1_out1, demultiplexer_1_out2, demultiplexer_1_out3,
       demultiplexer_1_out4, demultiplexer_1_out5, demultiplexer_1_out6, demultiplexer_1_out7;
  wire [15:0] Reg0, Reg1, Reg2, Reg3, Reg4, Reg5, Reg6, Reg7;

  Demultiplexer #(.select(3), .enable("false")) demultiplexer_1 (
    .out0(demultiplexer_1_out0), .out1(demultiplexer_1_out1), .out2(demultiplexer_1_out2),
    .out3(demultiplexer_1_out3), .out4(demultiplexer_1_out4), .out5(demultiplexer_1_out5),
    .out6(demultiplexer_1_out6), .out7(demultiplexer_1_out7), .in(WriteEnable), .sel(WriteReg));
  Register #(.width(16)) register_1 (.D(WriteData), .en(demultiplexer_1_out0), .Q(Reg0), .clk(Clock));  // open: clr
  Register #(.width(16)) register_2 (.D(WriteData), .en(demultiplexer_1_out1), .Q(Reg1), .clk(Clock));  // open: clr
  Register #(.width(16)) register_3 (.D(WriteData), .en(demultiplexer_1_out2), .Q(Reg2), .clk(Clock));  // open: clr
  Register #(.width(16)) register_4 (.D(WriteData), .en(demultiplexer_1_out3), .Q(Reg3), .clk(Clock));  // open: clr
  Register #(.width(16)) register_5 (.D(WriteData), .en(demultiplexer_1_out4), .Q(Reg4), .clk(Clock));  // open: clr
  Register #(.width(16)) register_6 (.D(WriteData), .en(demultiplexer_1_out5), .Q(Reg5), .clk(Clock));  // open: clr
  Register #(.width(16)) register_7 (.D(WriteData), .en(demultiplexer_1_out6), .Q(Reg6), .clk(Clock));  // open: clr
  Register #(.width(16)) register_8 (.D(WriteData), .en(demultiplexer_1_out7), .Q(Reg7), .clk(Clock));  // open: clr
  Multiplexer #(.select(3), .width(16), .enable("false")) multiplexer_1 (
    .in0(Reg0), .in1(Reg1), .in2(Reg2), .in3(Reg3), .in4(Reg4), .in5(Reg5), .in6(Reg6), .in7(Reg7),
    .out(RegData1), .sel(ReadReg1));
  Multiplexer #(.select(3), .width(16), .enable("false")) multiplexer_2 (
    .in0(Reg0), .in1(Reg1), .in2(Reg2), .in3(Reg3), .in4(Reg4), .in5(Reg5), .in6(Reg6), .in7(Reg7),
    .out(RegData2), .sel(ReadReg2));
endmodule

module ALU (
  input  [15:0] Input_A,
  input  [15:0] Input_B,
  input  [2:0] ALUControl,
  input  [3:0] SHAMT,
  output [15:0] ALUResult
);

  wire [15:0] adder_1_out, and_1_out, nor_1_out, Shift_Left_output, Shift_Right_output, subtractor_1_out;

  Adder #(.width(16)) adder_1 (.a(Input_A), .b(Input_B), .out(adder_1_out));  // open: cin, cout
  Subtractor #(.width(16)) subtractor_1 (.a(Input_A), .b(Input_B), .out(subtractor_1_out));  // open: bin, bout
  assign and_1_out = Input_A & Input_B;  // AND_Gate and_1, 16 bits wide
  ShiftLeft Shift_Left (.Input_A(Input_A), .SHAMT(SHAMT), .OUTPUT(Shift_Left_output));
  ShiftRight Shift_Right (.Input_A(Input_A), .SHAMT(SHAMT), .Output(Shift_Right_output));
  assign nor_1_out = ~(Input_A | Input_B);  // NOR_Gate nor_1, 16 bits wide
  Multiplexer #(.select(3), .width(16), .enable("false")) multiplexer_1 (
    .in0(nor_1_out), .in1(adder_1_out), .in2(subtractor_1_out), .in3(and_1_out), .in4(Shift_Left_output),
    .in5(Shift_Right_output), .in6(Input_A), .in7(Input_A), .out(ALUResult), .sel(ALUControl));

  // Notes on the sheet:
  //   Wire Drawing Won't Work unless in this configuration for whatever reason
endmodule

module ShiftLeft (
  input  [15:0] Input_A,
  input  [3:0] SHAMT,
  output [15:0] OUTPUT
);

  wire [15:0] shifter_1_out, shifter_2_out, shifter_3_out, shifter_4_out, shifter_5_out, shifter_6_out,
       shifter_7_out, shifter_8_out, shifter_9_out, shifter_10_out, shifter_11_out, shifter_12_out,
       shifter_13_out, shifter_14_out, shifter_15_out;

  Shifter #(.width(16)) shifter_1 (.in(Input_A), .\dist (4'b0001), .out(shifter_1_out));
  Multiplexer #(.select(4), .width(16), .enable("false")) multiplexer_1 (
    .in0(Input_A), .in1(shifter_1_out), .in2(shifter_2_out), .in3(shifter_3_out), .in4(shifter_4_out),
    .in5(shifter_5_out), .in6(shifter_6_out), .in7(shifter_7_out), .in8(shifter_8_out), .in9(shifter_9_out),
    .in10(shifter_10_out), .in11(shifter_11_out), .in12(shifter_12_out), .in13(shifter_13_out),
    .in14(shifter_14_out), .in15(shifter_15_out), .out(OUTPUT), .sel(SHAMT));
  Shifter #(.width(16)) shifter_2 (.in(shifter_1_out), .\dist (4'b0001), .out(shifter_2_out));
  Shifter #(.width(16)) shifter_3 (.in(shifter_2_out), .\dist (4'b0001), .out(shifter_3_out));
  Shifter #(.width(16)) shifter_4 (.in(shifter_3_out), .\dist (4'b0001), .out(shifter_4_out));
  Shifter #(.width(16)) shifter_5 (.in(shifter_4_out), .\dist (4'b0001), .out(shifter_5_out));
  Shifter #(.width(16)) shifter_6 (.in(shifter_5_out), .\dist (4'b0001), .out(shifter_6_out));
  Shifter #(.width(16)) shifter_7 (.in(shifter_6_out), .\dist (4'b0001), .out(shifter_7_out));
  Shifter #(.width(16)) shifter_8 (.in(shifter_7_out), .\dist (4'b0001), .out(shifter_8_out));
  Shifter #(.width(16)) shifter_9 (.in(shifter_8_out), .\dist (4'b0001), .out(shifter_9_out));
  Shifter #(.width(16)) shifter_10 (.in(shifter_9_out), .\dist (4'b0001), .out(shifter_10_out));
  Shifter #(.width(16)) shifter_11 (.in(shifter_10_out), .\dist (4'b0001), .out(shifter_11_out));
  Shifter #(.width(16)) shifter_12 (.in(shifter_11_out), .\dist (4'b0001), .out(shifter_12_out));
  Shifter #(.width(16)) shifter_13 (.in(shifter_12_out), .\dist (4'b0001), .out(shifter_13_out));
  Shifter #(.width(16)) shifter_14 (.in(shifter_13_out), .\dist (4'b0001), .out(shifter_14_out));
  Shifter #(.width(16)) shifter_15 (.in(shifter_14_out), .\dist (4'b0001), .out(shifter_15_out));
endmodule

module ShiftRight (
  input  [15:0] Input_A,
  input  [3:0] SHAMT,
  output [15:0] Output
);

  wire [15:0] shifter_1_out, shifter_2_out, shifter_3_out, shifter_4_out, shifter_5_out, shifter_6_out,
       shifter_7_out, shifter_8_out, shifter_9_out, shifter_10_out, shifter_11_out, shifter_12_out,
       shifter_13_out, shifter_14_out, shifter_15_out;

  Shifter #(.width(16), .shift("lr")) shifter_1 (.in(Input_A), .\dist (4'b0001), .out(shifter_1_out));
  Multiplexer #(.select(4), .width(16), .enable("false")) multiplexer_1 (
    .in0(Input_A), .in1(shifter_1_out), .in2(shifter_2_out), .in3(shifter_3_out), .in4(shifter_4_out),
    .in5(shifter_5_out), .in6(shifter_6_out), .in7(shifter_7_out), .in8(shifter_8_out), .in9(shifter_9_out),
    .in10(shifter_10_out), .in11(shifter_11_out), .in12(shifter_12_out), .in13(shifter_13_out),
    .in14(shifter_14_out), .in15(shifter_15_out), .out(Output), .sel(SHAMT));
  Shifter #(.width(16), .shift("lr")) shifter_2 (.in(shifter_1_out), .\dist (4'b0001), .out(shifter_2_out));
  Shifter #(.width(16), .shift("lr")) shifter_3 (.in(shifter_2_out), .\dist (4'b0001), .out(shifter_3_out));
  Shifter #(.width(16), .shift("lr")) shifter_4 (.in(shifter_3_out), .\dist (4'b0001), .out(shifter_4_out));
  Shifter #(.width(16), .shift("lr")) shifter_5 (.in(shifter_4_out), .\dist (4'b0001), .out(shifter_5_out));
  Shifter #(.width(16), .shift("lr")) shifter_6 (.in(shifter_5_out), .\dist (4'b0001), .out(shifter_6_out));
  Shifter #(.width(16), .shift("lr")) shifter_7 (.in(shifter_6_out), .\dist (4'b0001), .out(shifter_7_out));
  Shifter #(.width(16), .shift("lr")) shifter_8 (.in(shifter_7_out), .\dist (4'b0001), .out(shifter_8_out));
  Shifter #(.width(16), .shift("lr")) shifter_9 (.in(shifter_8_out), .\dist (4'b0001), .out(shifter_9_out));
  Shifter #(.width(16), .shift("lr")) shifter_10 (.in(shifter_9_out), .\dist (4'b0001), .out(shifter_10_out));
  Shifter #(.width(16), .shift("lr")) shifter_11 (.in(shifter_10_out), .\dist (4'b0001), .out(shifter_11_out));
  Shifter #(.width(16), .shift("lr")) shifter_12 (.in(shifter_11_out), .\dist (4'b0001), .out(shifter_12_out));
  Shifter #(.width(16), .shift("lr")) shifter_13 (.in(shifter_12_out), .\dist (4'b0001), .out(shifter_13_out));
  Shifter #(.width(16), .shift("lr")) shifter_14 (.in(shifter_13_out), .\dist (4'b0001), .out(shifter_14_out));
  Shifter #(.width(16), .shift("lr")) shifter_15 (.in(shifter_14_out), .\dist (4'b0001), .out(shifter_15_out));
endmodule

module Zero (
  input  [15:0] Input_A,
  output Output
);

  wire and_1_out, and_3_out, multiplexer_1_out, multiplexer_2_out, multiplexer_3_out, multiplexer_4_out;

  Multiplexer #(.select(4), .enable("false")) multiplexer_1 (
    .in0(1'b1), .in1(1'b0), .in2(1'b0), .in3(1'b0), .in4(1'b0), .in5(1'b0), .in6(1'b0), .in7(1'b0),
    .in8(1'b0), .in9(1'b0), .in10(1'b0), .in11(1'b0), .in12(1'b0), .in13(1'b0), .in14(1'b0), .in15(1'b0),
    .out(multiplexer_1_out), .sel(Input_A[15:12]));
  and and_1 (and_1_out, multiplexer_1_out, multiplexer_2_out);
  Multiplexer #(.select(4), .enable("false")) multiplexer_2 (
    .in0(1'b1), .in1(1'b0), .in2(1'b0), .in3(1'b0), .in4(1'b0), .in5(1'b0), .in6(1'b0), .in7(1'b0),
    .in8(1'b0), .in9(1'b0), .in10(1'b0), .in11(1'b0), .in12(1'b0), .in13(1'b0), .in14(1'b0), .in15(1'b0),
    .out(multiplexer_2_out), .sel(Input_A[11:8]));
  and and_2 (Output, and_1_out, and_3_out);
  Multiplexer #(.select(4), .enable("false")) multiplexer_3 (
    .in0(1'b1), .in1(1'b0), .in2(1'b0), .in3(1'b0), .in4(1'b0), .in5(1'b0), .in6(1'b0), .in7(1'b0),
    .in8(1'b0), .in9(1'b0), .in10(1'b0), .in11(1'b0), .in12(1'b0), .in13(1'b0), .in14(1'b0), .in15(1'b0),
    .out(multiplexer_3_out), .sel(Input_A[7:4]));
  and and_3 (and_3_out, multiplexer_3_out, multiplexer_4_out);
  Multiplexer #(.select(4), .enable("false")) multiplexer_4 (
    .in0(1'b1), .in1(1'b0), .in2(1'b0), .in3(1'b0), .in4(1'b0), .in5(1'b0), .in6(1'b0), .in7(1'b0),
    .in8(1'b0), .in9(1'b0), .in10(1'b0), .in11(1'b0), .in12(1'b0), .in13(1'b0), .in14(1'b0), .in15(1'b0),
    .out(multiplexer_4_out), .sel(Input_A[3:0]));
endmodule

module ALU_CONTROL (
  input  ALUOP1,
  input  ALUOP2,
  input  FUNCT,
  output ALUCONTROL1,
  output ALUCONTROL2,
  output ALUCONTROL3
);

  wire and_2_out, and_3_out, and_4_out, and_5_out, and_6_out, not_1_out, not_2_out, not_3_out, not_4_out,
       not_5_out, not_6_out, not_7_out, not_8_out;

  not not_1 (not_1_out, ALUOP2);
  not not_2 (not_2_out, ALUOP1);
  not not_3 (not_3_out, ALUOP2);
  not not_4 (not_4_out, ALUOP1);
  not not_5 (not_5_out, FUNCT);
  not not_6 (not_6_out, ALUOP1);
  not not_7 (not_7_out, FUNCT);
  not not_8 (not_8_out, FUNCT);
  and and_1 (ALUCONTROL1, ALUOP1, not_1_out);
  and and_2 (and_2_out, not_2_out, not_3_out, FUNCT);
  and and_3 (and_3_out, not_4_out, ALUOP2, not_5_out);
  and and_4 (and_4_out, not_6_out, not_7_out);
  and and_5 (and_5_out, ALUOP2, not_8_out);
  and and_6 (and_6_out, ALUOP1, FUNCT);
  or or_1 (ALUCONTROL2, and_2_out, and_3_out);
  or or_2 (ALUCONTROL3, and_4_out, and_5_out, and_6_out);
endmodule

module NotEqualToZero (
  input  [15:0] Input_A,
  output Output
);

  wire multiplexer_1_out, multiplexer_2_out, multiplexer_3_out, multiplexer_4_out, or_1_out, or_3_out;

  Multiplexer #(.select(4), .enable("false")) multiplexer_1 (
    .in0(1'b0), .in1(1'b1), .in2(1'b1), .in3(1'b1), .in4(1'b1), .in5(1'b1), .in6(1'b1), .in7(1'b1),
    .in8(1'b1), .in9(1'b1), .in10(1'b1), .in11(1'b1), .in12(1'b1), .in13(1'b1), .in14(1'b1), .in15(1'b1),
    .out(multiplexer_1_out), .sel(Input_A[15:12]));
  or or_1 (or_1_out, multiplexer_1_out, multiplexer_2_out);
  Multiplexer #(.select(4), .enable("false")) multiplexer_2 (
    .in0(1'b0), .in1(1'b1), .in2(1'b1), .in3(1'b1), .in4(1'b1), .in5(1'b1), .in6(1'b1), .in7(1'b1),
    .in8(1'b1), .in9(1'b1), .in10(1'b1), .in11(1'b1), .in12(1'b1), .in13(1'b1), .in14(1'b1), .in15(1'b1),
    .out(multiplexer_2_out), .sel(Input_A[11:8]));
  or or_2 (Output, or_1_out, or_3_out);
  Multiplexer #(.select(4), .enable("false")) multiplexer_3 (
    .in0(1'b0), .in1(1'b1), .in2(1'b1), .in3(1'b1), .in4(1'b1), .in5(1'b1), .in6(1'b1), .in7(1'b1),
    .in8(1'b1), .in9(1'b1), .in10(1'b1), .in11(1'b1), .in12(1'b1), .in13(1'b1), .in14(1'b1), .in15(1'b1),
    .out(multiplexer_3_out), .sel(Input_A[7:4]));
  or or_3 (or_3_out, multiplexer_3_out, multiplexer_4_out);
  Multiplexer #(.select(4), .enable("false")) multiplexer_4 (
    .in0(1'b0), .in1(1'b1), .in2(1'b1), .in3(1'b1), .in4(1'b1), .in5(1'b1), .in6(1'b1), .in7(1'b1),
    .in8(1'b1), .in9(1'b1), .in10(1'b1), .in11(1'b1), .in12(1'b1), .in13(1'b1), .in14(1'b1), .in15(1'b1),
    .out(multiplexer_4_out), .sel(Input_A[3:0]));
endmodule

module BranchControl (
  input  OP1,
  input  OP2,
  input  OP3,
  input  OP4,
  output BranchEqual,
  output BrancNotEqual
);

  wire and_2_out, and_3_out, not_1_out, not_2_out, not_3_out, not_4_out, not_5_out;

  and and_1 (BranchEqual, OP1, not_1_out, OP4);
  not not_1 (not_1_out, OP2);
  not not_2 (not_2_out, OP2);
  not not_3 (not_3_out, OP3);
  not not_4 (not_4_out, OP4);
  not not_5 (not_5_out, OP2);
  and and_2 (and_2_out, OP1, not_2_out, not_3_out, not_4_out);
  or or_1 (BrancNotEqual, and_2_out, and_3_out);
  and and_3 (and_3_out, OP1, not_5_out, OP3, OP4);
endmodule

module SignalControl (
  input  OP1,
  input  OP2,
  input  OP3,
  input  OP4,
  input  FUNCT,
  output ALUSRC,
  output ALUOP1,
  output ALUOP2,
  output RegWrite,
  output J,
  output JR,
  output JAL,
  output MemRead,
  output MemWrite,
  output MemToReg,
  output PUT,
  output HALT
);

  wire and_2_out, and_3_out, and_4_out, and_5_out, and_6_out, and_7_out, and_8_out, and_9_out, and_10_out,
       and_11_out, and_12_out, not_1_out, not_2_out, not_3_out, not_4_out, not_5_out, not_6_out, not_7_out,
       not_8_out, not_9_out, not_10_out, not_11_out, not_12_out, not_13_out, not_14_out, not_15_out,
       not_16_out, not_17_out, not_18_out, not_19_out, not_20_out, not_21_out, not_22_out, not_23_out,
       not_24_out, not_25_out, not_26_out, not_27_out, not_28_out, not_29_out, not_30_out, not_31_out,
       not_32_out, not_33_out, not_34_out, not_35_out, not_36_out, not_37_out, not_38_out;

  not not_1 (not_1_out, OP1);
  not not_2 (not_2_out, OP2);
  not not_3 (not_3_out, OP4);
  not not_4 (not_4_out, OP2);
  not not_5 (not_5_out, OP3);
  not not_6 (not_6_out, OP1);
  not not_7 (not_7_out, OP2);
  not not_8 (not_8_out, OP4);
  not not_9 (not_9_out, OP1);
  not not_10 (not_10_out, OP3);
  not not_11 (not_11_out, OP4);
  not not_12 (not_12_out, OP1);
  not not_13 (not_13_out, OP1);
  not not_14 (not_14_out, OP2);
  not not_15 (not_15_out, OP1);
  not not_16 (not_16_out, OP1);
  not not_17 (not_17_out, OP2);
  not not_18 (not_18_out, OP1);
  not not_19 (not_19_out, OP2);
  not not_20 (not_20_out, OP1);
  not not_21 (not_21_out, FUNCT);
  not not_22 (not_22_out, OP1);
  not not_23 (not_23_out, OP3);
  not not_24 (not_24_out, OP4);
  not not_25 (not_25_out, OP3);
  not not_26 (not_26_out, OP4);
  not not_27 (not_27_out, OP2);
  not not_28 (not_28_out, OP4);
  not not_29 (not_29_out, OP2);
  not not_30 (not_30_out, OP1);
  not not_31 (not_31_out, FUNCT);
  not not_32 (not_32_out, OP1);
  not not_33 (not_33_out, OP1);
  not not_34 (not_34_out, FUNCT);
  not not_35 (not_35_out, OP1);
  not not_36 (not_36_out, OP2);
  not not_37 (not_37_out, OP3);
  not not_38 (not_38_out, OP4);
  and and_1 (HALT, OP1, OP2, OP3, OP4);
  and and_2 (and_2_out, not_1_out, not_2_out, OP3, not_3_out);
  and and_3 (and_3_out, OP1, not_4_out, not_5_out);
  and and_4 (and_4_out, not_6_out, not_7_out, OP3, not_8_out, FUNCT);
  and and_5 (and_5_out, not_9_out, OP2, not_10_out, not_11_out);
  and and_6 (and_6_out, not_12_out, OP2, OP3, OP4);
  and and_7 (and_7_out, not_13_out, not_14_out, OP3, FUNCT);
  and and_8 (and_8_out, not_15_out, OP3, OP4);
  and and_9 (and_9_out, not_16_out, not_17_out, OP4);
  and and_10 (and_10_out, not_18_out, not_19_out, OP3);
  and and_11 (and_11_out, not_20_out, OP3, OP4, not_21_out);
  and and_12 (and_12_out, not_22_out, OP2, not_23_out, not_24_out);
  and and_13 (J, OP1, OP2, not_25_out, not_26_out);
  and and_14 (JR, OP1, not_27_out, OP3, not_28_out);
  and and_15 (JAL, OP1, not_29_out, OP3, OP4);
  and and_16 (MemRead, not_30_out, OP2, OP3, OP4, not_31_out);
  and and_17 (MemWrite, not_32_out, OP2, OP3, OP4, FUNCT);
  and and_18 (MemToReg, not_33_out, OP2, OP3, OP4, not_34_out);
  and and_19 (PUT, not_35_out, not_36_out, not_37_out, not_38_out);
  or or_1 (ALUSRC, and_2_out, and_3_out);
  or or_2 (ALUOP1, and_4_out, and_5_out, and_6_out);
  or or_3 (ALUOP2, and_7_out, and_8_out);
  or or_4 (RegWrite, and_9_out, and_10_out, and_11_out, and_12_out);
endmodule

module ADDI (
  input  [15:0] Register,
  input  [7:0] Immediate,
  output [15:0] Result,
  output BNE,
  output BEZ
);

  wire Signed_Output_sub;
  wire [7:0] Signed_Output_zero2;
  wire [15:0] adder_1_out, bit_extender_1_out, subtractor_1_out;

  assign bit_extender_1_out = {{8{1'b0}}, Immediate};  // Bit_Extender bit_extender_1
  signed_output Signed_Output (
    .seven(Immediate[7]), .six(Immediate[6]), .five(Immediate[5]), .four(Immediate[4]), .three(Immediate[3]),
    .two(Immediate[2]), .one(Immediate[1]), .zero(Immediate[0]), .seven2(Signed_Output_zero2[7]),
    .six2(Signed_Output_zero2[6]), .five2(Signed_Output_zero2[5]), .four2(Signed_Output_zero2[4]),
    .three2(Signed_Output_zero2[3]), .two2(Signed_Output_zero2[2]), .one2(Signed_Output_zero2[1]),
    .zero2(Signed_Output_zero2[0]), .sub(Signed_Output_sub));
  Adder #(.width(16)) adder_1 (.a(Register), .b(bit_extender_1_out), .out(adder_1_out));  // open: cin, cout
  Subtractor #(.width(16)) subtractor_1 (
    .a(Register), .b({{8{1'b0}}, Signed_Output_zero2}), .out(subtractor_1_out));  // open: bin, bout
  NotEqualToZero NotEqualToZero (.Input_A(Register), .Output(BNE));
  Zero Equal_To_Zero (.Input_A(Register), .Output(BEZ));
  Multiplexer #(.width(16), .enable("false")) multiplexer_1 (
    .in0(adder_1_out), .in1(subtractor_1_out), .out(Result), .sel(Signed_Output_sub));
endmodule

module ADDI_CONTROL (
  input  OP1,
  input  OP2,
  input  OP3,
  input  OP4,
  input  FUNCT,
  output ADDI
);

  wire not_1_out, not_2_out, not_3_out, not_4_out;

  not not_1 (not_1_out, OP1);
  not not_2 (not_2_out, OP2);
  not not_3 (not_3_out, OP4);
  not not_4 (not_4_out, FUNCT);
  and and_1 (ADDI, not_1_out, not_2_out, OP3, not_3_out, not_4_out);
endmodule

module signed_output (
  input  seven,
  input  six,
  input  five,
  input  four,
  input  three,
  input  two,
  input  one,
  input  zero,
  output seven2,
  output six2,
  output five2,
  output four2,
  output three2,
  output two2,
  output one2,
  output zero2,
  output sub
);

  wire and_2_out, and_3_out, and_4_out, and_5_out, and_6_out, and_7_out, and_8_out, and_9_out, and_10_out,
       and_11_out, and_12_out, and_13_out, and_14_out, and_15_out, and_16_out, and_17_out, and_18_out,
       and_19_out, and_20_out, and_21_out, and_22_out, and_23_out, and_24_out, and_25_out, and_26_out,
       and_27_out, and_28_out, and_29_out, and_30_out, and_31_out, and_32_out, and_33_out, and_34_out,
       and_35_out, and_36_out, not_1_out, not_2_out, not_3_out, not_4_out, not_5_out, not_6_out, not_7_out,
       not_8_out, not_9_out, not_10_out, not_11_out, not_12_out, not_13_out, not_14_out, not_15_out,
       not_16_out, not_17_out, not_18_out, not_19_out, not_20_out, not_21_out, not_22_out, not_23_out,
       not_24_out, not_25_out, not_26_out, not_27_out, not_28_out, not_29_out, not_30_out, not_31_out,
       not_32_out, not_33_out, not_34_out, not_35_out, not_36_out, not_37_out, not_38_out, not_39_out,
       not_40_out, not_41_out, not_42_out, not_43_out, not_44_out, not_45_out, not_46_out, not_47_out,
       not_48_out;

  and and_1 (seven2, seven, not_1_out);
  not not_1 (not_1_out, six);
  not not_2 (not_2_out, seven);
  and and_2 (and_2_out, not_2_out, six);
  and and_3 (and_3_out, six, not_3_out);
  not not_3 (not_3_out, five);
  not not_4 (not_4_out, seven);
  and and_4 (and_4_out, not_4_out, five, not_5_out);
  not not_5 (not_5_out, three);
  not not_6 (not_6_out, seven);
  and and_5 (and_5_out, not_6_out, five, not_7_out);
  not not_7 (not_7_out, two);
  not not_8 (not_8_out, seven);
  and and_6 (and_6_out, not_8_out, five, not_9_out);
  not not_9 (not_9_out, one);
  not not_10 (not_10_out, seven);
  and and_7 (and_7_out, not_10_out, five, not_11_out);
  not not_11 (not_11_out, zero);
  not not_12 (not_12_out, six);
  and and_8 (and_8_out, not_12_out, five);
  and and_9 (and_9_out, five, not_13_out);
  not not_13 (not_13_out, four);
  not not_14 (not_14_out, seven);
  and and_10 (and_10_out, not_14_out, four, not_15_out);
  not not_15 (not_15_out, two);
  not not_16 (not_16_out, seven);
  and and_11 (and_11_out, not_16_out, four, not_17_out);
  not not_17 (not_17_out, one);
  not not_18 (not_18_out, seven);
  and and_12 (and_12_out, not_18_out, four, not_19_out);
  not not_19 (not_19_out, zero);
  not not_20 (not_20_out, five);
  and and_13 (and_13_out, not_20_out, four);
  and and_14 (and_14_out, four, not_21_out);
  not not_21 (not_21_out, three);
  not not_22 (not_22_out, six);
  and and_15 (and_15_out, seven, not_22_out, four);
  not not_23 (not_23_out, seven);
  and and_16 (and_16_out, not_23_out, three, not_24_out);
  not not_24 (not_24_out, one);
  not not_25 (not_25_out, seven);
  and and_17 (and_17_out, not_25_out, three, not_26_out);
  not not_26 (not_26_out, zero);
  not not_27 (not_27_out, four);
  and and_18 (and_18_out, not_27_out, three);
  and and_19 (and_19_out, three, not_28_out);
  not not_28 (not_28_out, two);
  and and_20 (and_20_out, seven, not_29_out, three);
  not not_29 (not_29_out, six);
  and and_21 (and_21_out, seven, not_30_out, three);
  not not_30 (not_30_out, five);
  not not_31 (not_31_out, seven);
  and and_22 (and_22_out, not_31_out, two, not_32_out);
  not not_32 (not_32_out, zero);
  not not_33 (not_33_out, three);
  and and_23 (and_23_out, not_33_out, two);
  and and_24 (and_24_out, two, not_34_out);
  not not_34 (not_34_out, one);
  not not_35 (not_35_out, six);
  and and_25 (and_25_out, seven, not_35_out, two);
  and and_26 (and_26_out, seven, not_36_out, two);
  not not_36 (not_36_out, five);
  and and_27 (and_27_out, seven, not_37_out, two);
  not not_37 (not_37_out, four);
  not not_38 (not_38_out, two);
  and and_28 (and_28_out, not_38_out, one);
  and and_29 (and_29_out, one, not_39_out);
  not not_39 (not_39_out, zero);
  and and_30 (and_30_out, seven, not_40_out, one);
  not not_40 (not_40_out, six);
  not not_41 (not_41_out, five);
  and and_31 (and_31_out, seven, not_41_out, one);
  and and_32 (and_32_out, seven, not_42_out, one);
  not not_42 (not_42_out, four);
  and and_33 (and_33_out, seven, not_43_out, one);
  not not_43 (not_43_out, three);
  not not_44 (not_44_out, one);
  not not_45 (not_45_out, seven);
  not not_46 (not_46_out, six);
  not not_47 (not_47_out, five);
  not not_48 (not_48_out, one);
  or or_1 (six2, and_2_out, and_3_out);
  and and_34 (and_34_out, not_44_out, zero);
  and and_35 (and_35_out, not_45_out, not_46_out, not_47_out, four, three, two, not_48_out);
  and and_36 (and_36_out, seven, zero);
  or or_2 (five2, and_4_out, and_5_out, and_6_out, and_7_out, and_8_out, and_9_out);
  or or_3 (four2, and_10_out, and_11_out, and_12_out, and_13_out, and_14_out, and_15_out);
  or or_4 (three2, and_16_out, and_17_out, and_18_out, and_19_out, and_20_out, and_21_out);
  or or_5 (two2, and_22_out, and_23_out, and_24_out, and_25_out, and_26_out, and_27_out);
  or or_6 (one2, and_28_out, and_29_out, and_30_out, and_31_out, and_32_out, and_33_out);
  or or_7 (zero2, and_34_out, and_35_out, and_36_out);

  assign sub = seven;
endmodule

module SW_LW (
  input  A
);
endmodule
