// Logisim project Lab11-rlb97.circ as structural Verilog: 4 circuits, main circuit main
module main (
);

  wire clock_1_out, decoder_1_select, fields_1_register, not_1_out;
  wire [1:0] decoder_1_operation;
  wire [3:0] fields_1_opcode;
  wire [7:0] A_q, adder_1_out, alu_1_result, B_q, fields_1_immediate, multiplexer_1_out, PC_q;
  wire [15:0] rom_1_data;

  Register PC (.D(adder_1_out), .en(1'b1), .Q(PC_q), .clk(clock_1_out));  // open: clr
  Clock clock_1 (.out(clock_1_out));
  Adder adder_1 (.a(PC_q), .b(8'h1), .out(adder_1_out), .cin(1'b0));  // open: cout
  ROM #(.dataWidth(16)) rom_1 (.addr(PC_q), .data(rom_1_data), .sel(1'b1));
  not not_1 (not_1_out, fields_1_register);
  Fields fields_1 (
    .Instruction(rom_1_data), .Immediate(fields_1_immediate), .Register(fields_1_register),
    .OpCode(fields_1_opcode));
  Register A (.D(multiplexer_1_out), .en(not_1_out), .Q(A_q), .clk(clock_1_out));  // open: clr
  Register B (.D(multiplexer_1_out), .en(fields_1_register), .Q(B_q), .clk(clock_1_out));  // open: clr
  Decoder decoder_1 (.Opcode(fields_1_opcode), .Operation(decoder_1_operation), .Select(decoder_1_select));
  ALU alu_1 (.A(A_q), .B(B_q), .Operation(decoder_1_operation), .Result(alu_1_result));
  Multiplexer #(.width(8), .enable("false")) multiplexer_1 (
    .in0(alu_1_result), .in1(fields_1_immediate), .out(multiplexer_1_out), .sel(decoder_1_select));

  // Notes on the sheet:
  //   Randyll Bearer Lab11
  //   contents of rom_1 (hex, n*v repeats v):
  //   1 802
endmodule

module ALU (
  input  [7:0] A,
  input  [7:0] B,
  input  [1:0] Operation,
  output [7:0] Result
);

  wire [7:0] adder_1_out, and_1_out, or_1_out, subtractor_1_out;

  Adder adder_1 (.a(A), .b(B), .out(adder_1_out), .cin(1'b0));  // open: cout
  Subtractor subtractor_1 (.a(A), .b(B), .out(subtractor_1_out), .bin(1'b0));  // open: bout
  assign or_1_out = A | B;  // OR_Gate or_1, 8 bits wide
  assign and_1_out = A & B;  // AND_Gate and_1, 8 bits wide
  Multiplexer #(.select(2), .width(8), .enable("false")) multiplexer_1 (
    .in0(adder_1_out), .in1(subtractor_1_out), .in2(or_1_out), .in3(and_1_out), .out(Result), .sel(Operation));
endmodule

module Fields (
  input  [15:0] Instruction,
  output [7:0] Immediate,
  output Register,
  output [3:0] OpCode
);


  assign Immediate = Instruction[7:0];
  assign OpCode = Instruction[15:12];
  assign Register = Instruction[11];
endmodule

module Decoder (
  input  [3:0] Opcode,
  output [1:0] Operation,
  output Select
);

  wire not_1_out, not_2_out, not_3_out;

  not not_1 (not_1_out, Opcode[1]);
  not not_2 (not_2_out, Opcode[2]);
  not not_3 (not_3_out, Opcode[1]);
  and and_1 (Select, not_2_out, not_3_out);

  assign Operation[0] = Opcode[0];
endmodule
