// Logisim project Lab09Part2-rlb97.circ as structural Verilog: 2 circuits, main circuit main
module main (
);

  wire button_1_out, button_2_out, button_3_out, button_4_out, button_5_out, button_6_out, Clock_out,
       cookiewatcher_1_cookiesburnt, cookiewatcher_1_cookiesdone, cookiewatcher_2_cookiesburnt,
       cookiewatcher_2_cookiesdone, cookiewatcher_3_cookiesburnt, cookiewatcher_3_cookiesdone,
       cookiewatcher_4_cookiesburnt, cookiewatcher_4_cookiesdone, cookiewatcher_5_cookiesburnt,
       cookiewatcher_5_cookiesdone, cookiewatcher_6_cookiesburnt, cookiewatcher_6_cookiesdone;

  Clock Clock (.out(Clock_out));
  Button button_1 (.out(button_1_out));
  Button button_2 (.out(button_2_out));
  Button button_3 (.out(button_3_out));
  Button button_4 (.out(button_4_out));
  Button button_5 (.out(button_5_out));
  Button button_6 (.out(button_6_out));
  LED led_1 (.in(cookiewatcher_1_cookiesburnt));
  CookieWatcher cookiewatcher_1 (
    .Clock(Clock_out), .BatchHandled(button_1_out), .CookiesBurnt(cookiewatcher_1_cookiesburnt),
    .CookiesDone(cookiewatcher_1_cookiesdone));
  LED led_2 (.in(cookiewatcher_1_cookiesdone));
  LED led_3 (.in(cookiewatcher_2_cookiesburnt));
  CookieWatcher cookiewatcher_2 (
    .Clock(Clock_out), .BatchHandled(button_2_out), .CookiesBurnt(cookiewatcher_2_cookiesburnt),
    .CookiesDone(cookiewatcher_2_cookiesdone));
  LED led_4 (.in(cookiewatcher_2_cookiesdone));
  CookieWatcher cookiewatcher_3 (
    .Clock(Clock_out), .BatchHandled(button_3_out), .CookiesBurnt(cookiewatcher_3_cookiesburnt),
    .CookiesDone(cookiewatcher_3_cookiesdone));
  LED led_5 (.in(cookiewatcher_3_cookiesburnt));
  LED led_6 (.in(cookiewatcher_3_cookiesdone));
  LED led_7 (.in(cookiewatcher_4_cookiesburnt));
  CookieWatcher cookiewatcher_4 (
    .Clock(Clock_out), .BatchHandled(button_4_out), .CookiesBurnt(cookiewatcher_4_cookiesburnt),
    .CookiesDone(cookiewatcher_4_cookiesdone));
  LED led_8 (.in(cookiewatcher_4_cookiesdone));
  LED led_9 (.in(cookiewatcher_5_cookiesburnt));
  CookieWatcher cookiewatcher_5 (
    .Clock(Clock_out), .BatchHandled(button_5_out), .CookiesBurnt(cookiewatcher_5_cookiesburnt),
    .CookiesDone(cookiewatcher_5_cookiesdone));
  LED led_10 (.in(cookiewatcher_5_cookiesdone));
  LED led_11 (.in(cookiewatcher_6_cookiesburnt));
  CookieWatcher cookiewatcher_6 (
    .Clock(Clock_out), .BatchHandled(button_6_out), .CookiesBurnt(cookiewatcher_6_cookiesburnt),
    .CookiesDone(cookiewatcher_6_cookiesdone));
  LED led_12 (.in(cookiewatcher_6_cookiesdone));

  // Notes on the sheet:
  //   Batch 1 
  //   Batch 2
  //   Batch 3
  //   Batch 4
  //   Batch 5
  //   Batch 6
endmodule

module CookieWatcher (
  input  Clock,
  input  BatchHandled,
  output CookiesBurnt,
  output CookiesDone
);

  wire [8:0] counter_1_q;

  Counter #(.width(10), .max('h3ff)) counter_1 (
    .load(1'b0), .count(1'b1), .Q({CookiesDone, counter_1_q}), .clk(Clock), .clr(BatchHandled));  // open: D, carry
  and and_1 (CookiesBurnt, counter_1_q[8], CookiesDone);
endmodule
