// Logisim project Project2-rlb97(TAKE2)Pre-SignalConnection.circ as structural Verilog
module main (
  input  [15:0] in_1,
  output out_2,
  output out_3,
  output out_4,
  output out_5
);

  wire ALU_equaltozero, ALU_notequaltozero, BEQ_out, BNE_out, Branch_Control_p6, Branch_out, clock_1_out,
       d_ff_1_q, signalcontrol_1_p6, undriven, undriven_2, undriven_3, undriven_4, undriven_6, undriven_7,
       undriven_8, undriven_9, undriven_10, undriven_11;
  wire [1:0] undriven_5;
  wire [2:0] ALU_CONTROL_alucontrol1;
  wire [3:0] Display_Register_q_2, signalcontrol_1_p1;
  wire [7:0] adder_1_out, adder_3_out, bit_extender_3_out, multiplexer_3_out, multiplexer_4_out,
       multiplexer_5_out, PC_q;
  wire [11:0] signalcontrol_1_p5;
  wire [15:0] adder_2_out, ALU_aluresult, bit_extender_1_out, bit_extender_2_out, Display_Register_q,
       multiplexer_1_out, multiplexer_2_out, multiplexer_6_out, ram_1_data, Register_Memory_regdata1,
       Register_Memory_regdata2;

  D_Flip_Flop d_ff_1 (.clk(clock_1_out), .Q(d_ff_1_q));  // open: D, Qn, preset, en, reset
  Clock clock_1 (.out(clock_1_out));
  Register PC (.D(multiplexer_5_out), .en(undriven), .Q(PC_q));  // open: clk, clr
  Adder adder_1 (.a(PC_q), .b(8'h1), .out(adder_1_out));  // open: cin, cout
  // SignalControl signalcontrol_1: pin names not known; wires that end beside it: signalcontrol_1_p1[0], signalcontrol_1_p1[1], signalcontrol_1_p1[2], signalcontrol_1_p1[3], signalcontrol_1_p5[0], signalcontrol_1_p6
  // BranchControl Branch_Control: pin names not known; wires that end beside it: signalcontrol_1_p1[0], signalcontrol_1_p1[1], signalcontrol_1_p1[2], signalcontrol_1_p1[3], signalcontrol_1_p6, Branch_Control_p6
  assign bit_extender_1_out = {{8{1'b0}}, PC_q};  // Bit_Extender bit_extender_1
  ROM #(.dataWidth(16)) rom_1 (.addr(PC_q), .data({signalcontrol_1_p1, signalcontrol_1_p5}));  // open: sel
  Adder #(.width(16)) adder_2 (.a(bit_extender_1_out), .b(16'h1), .out(adder_2_out));  // open: cin, cout
  Multiplexer #(.width(16), .enable("false")) multiplexer_1 (
    .in0(multiplexer_6_out), .in1(adder_2_out), .out(multiplexer_1_out));  // open: sel
  Register_Memory Register_Memory (
    .ReadReg1(signalcontrol_1_p5[11:9]), .ReadReg2(signalcontrol_1_p5[8:6]),
    .WriteReg(signalcontrol_1_p5[11:9]), .WriteData(multiplexer_1_out), .WriteEnable(undriven_2),
    .Clock(undriven_3), .RegData1(Register_Memory_regdata1), .RegData2(Register_Memory_regdata2));
  assign bit_extender_2_out = {{8{1'b0}}, signalcontrol_1_p5[8:1]};  // Bit_Extender bit_extender_2
  Adder adder_3 (.a(8'h1), .b(signalcontrol_1_p5[8:1]), .out(adder_3_out));  // open: cin, cout
  Multiplexer #(.width(16), .enable("false")) multiplexer_2 (
    .in0(Register_Memory_regdata2), .in1(bit_extender_2_out), .out(multiplexer_2_out), .sel(undriven_4));
  ALU ALU (
    .Input_A(Register_Memory_regdata1), .Input_B(multiplexer_2_out), .SHAMT(signalcontrol_1_p5[4:1]),
    .ALUControl(ALU_CONTROL_alucontrol1), .NotEqualToZero(ALU_notequaltozero), .EqualToZero(ALU_equaltozero),
    .ALUResult(ALU_aluresult));
  ALU_CONTROL ALU_CONTROL (
    .ALUOP1(undriven_5[0]), .ALUOP2(undriven_5[1]), .FUNCT(signalcontrol_1_p5[0]),
    .ALUCONTROL1(ALU_CONTROL_alucontrol1[0]), .ALUCONTROL2(ALU_CONTROL_alucontrol1[1]),
    .ALUCONTROL3(ALU_CONTROL_alucontrol1[2]));
  Multiplexer #(.width(8), .enable("false")) multiplexer_3 (
    .in0(adder_1_out), .in1(adder_3_out), .out(multiplexer_3_out), .sel(Branch_out));
  or Branch (Branch_out, BEQ_out, BNE_out);
  and BEQ (BEQ_out, signalcontrol_1_p6, ALU_equaltozero);
  and BNE (BNE_out, Branch_Control_p6, ALU_notequaltozero);
  Multiplexer #(.width(8), .enable("false")) multiplexer_4 (
    .in0(multiplexer_3_out), .in1(signalcontrol_1_p5[8:1]), .out(multiplexer_4_out));  // open: sel
  Bit_Extender #(.in_width(16), .out_width(8)) bit_extender_3 (.in(Register_Memory_regdata1), .out(bit_extender_3_out));
  RAM #(.addrWidth(16), .dataWidth(16), .bus("separate")) ram_1 (
    .addr(Register_Memory_regdata2), .din(ALU_aluresult), .data(ram_1_data), .str(undriven_6),
    .sel(undriven_7), .ld(undriven_8));  // open: clk, clr
  Multiplexer #(.width(8), .disabled(0), .enable("false")) multiplexer_5 (
    .in0(multiplexer_4_out), .in1(bit_extender_3_out), .out(multiplexer_5_out));  // open: sel
  Multiplexer #(.width(16), .enable("false")) multiplexer_6 (
    .in0(ALU_aluresult), .in1(ram_1_data), .out(multiplexer_6_out), .sel(undriven_10));
  Register #(.width(16)) Display_Register (
    .D(Register_Memory_regdata1), .en(undriven_9),
    .Q({Display_Register_q[15:8], Display_Register_q_2, Display_Register_q[3:0]}), .clk(undriven_11));  // open: clr
  LED Halt_LED ();  // open: in
  Hex_Digit_Display hex_digit_display_1 (.value(Display_Register_q[15:12]));  // open: dp
  Hex_Digit_Display hex_digit_display_2 (.value(Display_Register_q[11:8]));  // open: dp
  Hex_Digit_Display hex_digit_display_3 (.value(Display_Register_q_2));  // open: dp
  Hex_Digit_Display hex_digit_display_4 (.value(Display_Register_q[3:0]));  // open: dp

  assign out_2 = in_1[12];
  assign out_3 = in_1[13];
  assign out_4 = in_1[14];
  assign out_5 = in_1[15];

  // Notes on the sheet:
  //   PC+1
  //   Instruction Memory
  //   JAL/Normal
  //   Jump
  //   Immediate
  //   Branch/PC+1
  //   Data Memory
  //   Jump/Whatever
  //   JR/Whatever
endmodule

module Register_Memory (
  input  WriteEnable,
  input  [2:0] ReadReg1,
  input  [2:0] ReadReg2,
  input  [2:0] WriteReg,
  input  [15:0] WriteData,
  input  Clock,
  output [15:0] RegData1,
  output [15:0] RegData2
);

  wire demultiplexer_1_out0, demultiplexer_1_out1, demultiplexer_1_out2, demultiplexer_1_out3,
       demultiplexer_1_out4, demultiplexer_1_out5, demultiplexer_1_out6, demultiplexer_1_out7;
  wire [15:0] Reg0, Reg1, Reg2, Reg3, Reg4, Reg5, Reg6, Reg7;

  Demultiplexer #(.select(3), .enable("false")) demultiplexer_1 (
    .out0(demultiplexer_1_out0), .out1(demultiplexer_1_out1), .out2(demultiplexer_1_out2),
    .out3(demultiplexer_1_out3), .out4(demultiplexer_1_out4), .out5(demultiplexer_1_out5),
    .out6(demultiplexer_1_out6), .out7(demultiplexer_1_out7), .in(WriteEnable), .sel(WriteReg));
  Register #(.width(16)) register_1 (.D(WriteData), .en(demultiplexer_1_out0), .Q(Reg0), .clk(Clock));  // open: clr
  Register #(.width(16)) register_2 (.D(WriteData), .en(demultiplexer_1_out1), .Q(Reg1), .clk(Clock));  // open: clr
  Register #(.width(16)) register_3 (.D(WriteData), .en(demultiplexer_1_out2), .Q(Reg2), .clk(Clock));  // open: clr
  Register #(.width(16)) register_4 (.D(WriteData), .en(demultiplexer_1_out3), .Q(Reg3), .clk(Clock));  // open: clr
  Register #(.width(16)) register_5 (.D(WriteData), .en(demultiplexer_1_out4), .Q(Reg4), .clk(Clock));  // open: clr
  Register #(.width(16)) register_6 (.D(WriteData), .en(demultiplexer_1_out5), .Q(Reg5), .clk(Clock));  // open: clr
  Register #(.width(16)) register_7 (.D(WriteData), .en(demultiplexer_1_out6), .Q(Reg6), .clk(Clock));  // open: clr
  Register #(.width(16)) register_8 (.D(WriteData), .en(demultiplexer_1_out7), .Q(Reg7), .clk(Clock));  // open: clr
  Multiplexer #(.select(3), .width(16), .enable("false")) multiplexer_1 (
    .in0(Reg0), .in1(Reg1), .in2(Reg2), .in3(Reg3), .in4(Reg4), .in5(Reg5), .in6(Reg6), .in7(Reg7),
    .out(RegData1), .sel(ReadReg1));
  Multiplexer #(.select(3), .width(16), .enable("false")) multiplexer_2 (
    .in0(Reg0), .in1(Reg1), .in2(Reg2), .in3(Reg3), .in4(Reg4), .in5(Reg5), .in6(Reg6), .in7(Reg7),
    .out(RegData2), .sel(ReadReg2));
endmodule

module ALU (
  input  [15:0] Input_A,
  input  [15:0] Input_B,
  input  [2:0] ALUControl,
  input  [3:0] SHAMT,
  output NotEqualToZero,
  output EqualToZero,
  output [15:0] ALUResult
);

  wire [15:0] adder_1_out, and_1_out, nor_1_out, Shift_Left_output, Shift_Right_output, subtractor_1_out;

  NotEqualToZero notequaltozero_1 (.Input_A(Input_A), .Input_B(Input_B), .Output(NotEqualToZero));
  Zero u_EqualToZero (.Input_A(Input_A), .Input_B(Input_B), .Output(EqualToZero));
  Adder #(.width(16)) adder_1 (.a(Input_A), .b(Input_B), .out(adder_1_out));  // open: cin, cout
  Subtractor #(.width(16)) subtractor_1 (.a(Input_A), .b(Input_B), .out(subtractor_1_out));  // open: bin, bout
  assign and_1_out = Input_A & Input_B;  // AND_Gate and_1, 16 bits wide
  ShiftLeft Shift_Left (.Input_A(Input_A), .SHAMT(SHAMT), .OUTPUT(Shift_Left_output));
  ShiftRight Shift_Right (.Input_A(Input_A), .SHAMT(SHAMT), .Output(Shift_Right_output));
  assign nor_1_out = ~(Input_A | Input_B);  // NOR_Gate nor_1, 16 bits wide
  Multiplexer #(.select(3), .width(16), .enable("false")) multiplexer_1 (
    .in0(nor_1_out), .in1(adder_1_out), .in2(subtractor_1_out), .in3(and_1_out), .in4(Shift_Left_output),
    .in5(Shift_Right_output), .in6(Input_A), .in7(Input_A), .out(ALUResult), .sel(ALUControl));

  // Notes on the sheet:
  //   Wire Drawing Won't Work unless in this configuration for whatever reason
endmodule

module ShiftLeft (
  input  [15:0] Input_A,
  input  [3:0] SHAMT,
  output [15:0] OUTPUT
);

  wire [15:0] shifter_1_out, shifter_2_out, shifter_3_out, shifter_4_out, shifter_5_out, shifter_6_out,
       shifter_7_out, shifter_8_out, shifter_9_out, shifter_10_out, shifter_11_out, shifter_12_out,
       shifter_13_out, shifter_14_out, shifter_15_out;

  Shifter #(.width(16)) shifter_1 (.in(Input_A), .\dist (4'b0001), .out(shifter_1_out));
  Multiplexer #(.select(4), .width(16), .enable("false")) multiplexer_1 (
    .in0(Input_A), .in1(shifter_1_out), .in2(shifter_2_out), .in3(shifter_3_out), .in4(shifter_4_out),
    .in5(shifter_5_out), .in6(shifter_6_out), .in7(shifter_7_out), .in8(shifter_8_out), .in9(shifter_9_out),
    .in10(shifter_10_out), .in11(shifter_11_out), .in12(shifter_12_out), .in13(shifter_13_out),
    .in14(shifter_14_out), .in15(shifter_15_out), .out(OUTPUT), .sel(SHAMT));
  Shifter #(.width(16)) shifter_2 (.in(shifter_1_out), .\dist (4'b0001), .out(shifter_2_out));
  Shifter #(.width(16)) shifter_3 (.in(shifter_2_out), .\dist (4'b0001), .out(shifter_3_out));
  Shifter #(.width(16)) shifter_4 (.in(shifter_3_out), .\dist (4'b0001), .out(shifter_4_out));
  Shifter #(.width(16)) shifter_5 (.in(shifter_4_out), .\dist (4'b0001), .out(shifter_5_out));
  Shifter #(.width(16)) shifter_6 (.in(shifter_5_out), .\dist (4'b0001), .out(shifter_6_out));
  Shifter #(.width(16)) shifter_7 (.in(shifter_6_out), .\dist (4'b0001), .out(shifter_7_out));
  Shifter #(.width(16)) shifter_8 (.in(shifter_7_out), .\dist (4'b0001), .out(shifter_8_out));
  Shifter #(.width(16)) shifter_9 (.in(shifter_8_out), .\dist (4'b0001), .out(shifter_9_out));
  Shifter #(.width(16)) shifter_10 (.in(shifter_9_out), .\dist (4'b0001), .out(shifter_10_out));
  Shifter #(.width(16)) shifter_11 (.in(shifter_10_out), .\dist (4'b0001), .out(shifter_11_out));
  Shifter #(.width(16)) shifter_12 (.in(shifter_11_out), .\dist (4'b0001), .out(shifter_12_out));
  Shifter #(.width(16)) shifter_13 (.in(shifter_12_out), .\dist (4'b0001), .out(shifter_13_out));
  Shifter #(.width(16)) shifter_14 (.in(shifter_13_out), .\dist (4'b0001), .out(shifter_14_out));
  Shifter #(.width(16)) shifter_15 (.in(shifter_14_out), .\dist (4'b0001), .out(shifter_15_out));
endmodule

module ShiftRight (
  input  [15:0] Input_A,
  input  [3:0] SHAMT,
  output [15:0] Output
);

  wire [15:0] shifter_1_out, shifter_2_out, shifter_3_out, shifter_4_out, shifter_5_out, shifter_6_out,
       shifter_7_out, shifter_8_out, shifter_9_out, shifter_10_out, shifter_11_out, shifter_12_out,
       shifter_13_out, shifter_14_out, shifter_15_out;

  Shifter #(.width(16), .shift("lr")) shifter_1 (.in(Input_A), .\dist (4'b0001), .out(shifter_1_out));
  Multiplexer #(.select(4), .width(16), .enable("false")) multiplexer_1 (
    .in0(Input_A), .in1(shifter_1_out), .in2(shifter_2_out), .in3(shifter_3_out), .in4(shifter_4_out),
    .in5(shifter_5_out), .in6(shifter_6_out), .in7(shifter_7_out), .in8(shifter_8_out), .in9(shifter_9_out),
    .in10(shifter_10_out), .in11(shifter_11_out), .in12(shifter_12_out), .in13(shifter_13_out),
    .in14(shifter_14_out), .in15(shifter_15_out), .out(Output), .sel(SHAMT));
  Shifter #(.width(16), .shift("lr")) shifter_2 (.in(shifter_1_out), .\dist (4'b0001), .out(shifter_2_out));
  Shifter #(.width(16), .shift("lr")) shifter_3 (.in(shifter_2_out), .\dist (4'b0001), .out(shifter_3_out));
  Shifter #(.width(16), .shift("lr")) shifter_4 (.in(shifter_3_out), .\dist (4'b0001), .out(shifter_4_out));
  Shifter #(.width(16), .shift("lr")) shifter_5 (.in(shifter_4_out), .\dist (4'b0001), .out(shifter_5_out));
  Shifter #(.width(16), .shift("lr")) shifter_6 (.in(shifter_5_out), .\dist (4'b0001), .out(shifter_6_out));
  Shifter #(.width(16), .shift("lr")) shifter_7 (.in(shifter_6_out), .\dist (4'b0001), .out(shifter_7_out));
  Shifter #(.width(16), .shift("lr")) shifter_8 (.in(shifter_7_out), .\dist (4'b0001), .out(shifter_8_out));
  Shifter #(.width(16), .shift("lr")) shifter_9 (.in(shifter_8_out), .\dist (4'b0001), .out(shifter_9_out));
  Shifter #(.width(16), .shift("lr")) shifter_10 (.in(shifter_9_out), .\dist (4'b0001), .out(shifter_10_out));
  Shifter #(.width(16), .shift("lr")) shifter_11 (.in(shifter_10_out), .\dist (4'b0001), .out(shifter_11_out));
  Shifter #(.width(16), .shift("lr")) shifter_12 (.in(shifter_11_out), .\dist (4'b0001), .out(shifter_12_out));
  Shifter #(.width(16), .shift("lr")) shifter_13 (.in(shifter_12_out), .\dist (4'b0001), .out(shifter_13_out));
  Shifter #(.width(16), .shift("lr")) shifter_14 (.in(shifter_13_out), .\dist (4'b0001), .out(shifter_14_out));
  Shifter #(.width(16), .shift("lr")) shifter_15 (.in(shifter_14_out), .\dist (4'b0001), .out(shifter_15_out));
endmodule

module Zero (
  input  [15:0] Input_A,
  input  [15:0] Input_B,
  output Output
);

  wire multiplexer_1_out, multiplexer_2_out, multiplexer_3_out, multiplexer_4_out, or_1_out, or_3_out;
  wire [3:0] subtractor_1_out;
  wire [15:4] subtractor_1_out_2;

  Subtractor #(.width(16)) subtractor_1 (
    .a(Input_A), .b(Input_B), .out({subtractor_1_out_2, subtractor_1_out}));  // open: bin, bout
  Multiplexer #(.select(4), .enable("false")) multiplexer_1 (
    .in0(1'b1), .in1(1'b0), .in2(1'b0), .in3(1'b0), .in4(1'b0), .in5(1'b0), .in6(1'b0), .in7(1'b0),
    .in8(1'b0), .in9(1'b0), .in10(1'b0), .in11(1'b0), .in12(1'b0), .in13(1'b0), .in14(1'b0), .in15(1'b0),
    .out(multiplexer_1_out), .sel(subtractor_1_out_2[15:12]));
  or or_1 (or_1_out, multiplexer_1_out, multiplexer_2_out);
  Multiplexer #(.select(4), .enable("false")) multiplexer_2 (
    .in0(1'b1), .in1(1'b0), .in2(1'b0), .in3(1'b0), .in4(1'b0), .in5(1'b0), .in6(1'b0), .in7(1'b0),
    .in8(1'b0), .in9(1'b0), .in10(1'b0), .in11(1'b0), .in12(1'b0), .in13(1'b0), .in14(1'b0), .in15(1'b0),
    .out(multiplexer_2_out), .sel(subtractor_1_out_2[11:8]));
  or or_2 (Output, or_1_out, or_3_out);
  Multiplexer #(.select(4), .enable("false")) multiplexer_3 (
    .in0(1'b1), .in1(1'b0), .in2(1'b0), .in3(1'b0), .in4(1'b0), .in5(1'b0), .in6(1'b0), .in7(1'b0),
    .in8(1'b0), .in9(1'b0), .in10(1'b0), .in11(1'b0), .in12(1'b0), .in13(1'b0), .in14(1'b0), .in15(1'b0),
    .out(multiplexer_3_out), .sel(subtractor_1_out_2[7:4]));
  or or_3 (or_3_out, multiplexer_3_out, multiplexer_4_out);
  Multiplexer #(.select(4), .enable("false")) multiplexer_4 (
    .in0(1'b1), .in1(1'b0), .in2(1'b0), .in3(1'b0), .in4(1'b0), .in5(1'b0), .in6(1'b0), .in7(1'b0),
    .in8(1'b0), .in9(1'b0), .in10(1'b0), .in11(1'b0), .in12(1'b0), .in13(1'b0), .in14(1'b0), .in15(1'b0),
    .out(multiplexer_4_out), .sel(subtractor_1_out));
endmodule

module ALU_CONTROL (
  input  ALUOP1,
  input  ALUOP2,
  input  FUNCT,
  output ALUCONTROL1,
  output ALUCONTROL2,
  output ALUCONTROL3
);

  wire and_2_out, and_3_out, and_4_out, and_5_out, and_6_out, not_1_out, not_2_out, not_3_out, not_4_out,
       not_5_out, not_6_out, not_7_out, not_8_out;

  not not_1 (not_1_out, ALUOP2);
  not not_2 (not_2_out, ALUOP1);
  not not_3 (not_3_out, ALUOP2);
  not not_4 (not_4_out, ALUOP1);
  not not_5 (not_5_out, FUNCT);
  not not_6 (not_6_out, ALUOP1);
  not not_7 (not_7_out, FUNCT);
  not not_8 (not_8_out, FUNCT);
  and and_1 (ALUCONTROL1, ALUOP1, not_1_out);
  and and_2 (and_2_out, not_2_out, not_3_out, FUNCT);
  and and_3 (and_3_out, not_4_out, ALUOP2, not_5_out);
  and and_4 (and_4_out, not_6_out, not_7_out);
  and and_5 (and_5_out, ALUOP2, not_8_out);
  and and_6 (and_6_out, ALUOP1, FUNCT);
  or or_1 (ALUCONTROL2, and_2_out, and_3_out);
  or or_2 (ALUCONTROL3, and_4_out, and_5_out, and_6_out);
endmodule

module NotEqualToZero (
  input  [15:0] Input_A,
  input  [15:0] Input_B,
  output Output
);

  wire multiplexer_1_out, multiplexer_2_out, multiplexer_3_out, multiplexer_4_out, or_1_out, or_3_out;
  wire [3:0] subtractor_1_out;
  wire [15:4] subtractor_1_out_2;

  Subtractor #(.width(16)) subtractor_1 (
    .a(Input_A), .b(Input_B), .out({subtractor_1_out_2, subtractor_1_out}));  // open: bin, bout
  Multiplexer #(.select(4), .enable("false")) multiplexer_1 (
    .in0(1'b0), .in1(1'b1), .in2(1'b1), .in3(1'b1), .in4(1'b1), .in5(1'b1), .in6(1'b1), .in7(1'b1),
    .in8(1'b1), .in9(1'b1), .in10(1'b1), .in11(1'b1), .in12(1'b1), .in13(1'b1), .in14(1'b1), .in15(1'b1),
    .out(multiplexer_1_out), .sel(subtractor_1_out_2[15:12]));
  or or_1 (or_1_out, multiplexer_1_out, multiplexer_2_out);
  Multiplexer #(.select(4), .enable("false")) multiplexer_2 (
    .in0(1'b0), .in1(1'b1), .in2(1'b1), .in3(1'b1), .in4(1'b1), .in5(1'b1), .in6(1'b1), .in7(1'b1),
    .in8(1'b1), .in9(1'b1), .in10(1'b1), .in11(1'b1), .in12(1'b1), .in13(1'b1), .in14(1'b1), .in15(1'b1),
    .out(multiplexer_2_out), .sel(subtractor_1_out_2[11:8]));
  or or_2 (Output, or_1_out, or_3_out);
  Multiplexer #(.select(4), .enable("false")) multiplexer_3 (
    .in0(1'b0), .in1(1'b1), .in2(1'b1), .in3(1'b1), .in4(1'b1), .in5(1'b1), .in6(1'b1), .in7(1'b1),
    .in8(1'b1), .in9(1'b1), .in10(1'b1), .in11(1'b1), .in12(1'b1), .in13(1'b1), .in14(1'b1), .in15(1'b1),
    .out(multiplexer_3_out), .sel(subtractor_1_out_2[7:4]));
  or or_3 (or_3_out, multiplexer_3_out, multiplexer_4_out);
  Multiplexer #(.select(4), .enable("false")) multiplexer_4 (
    .in0(1'b0), .in1(1'b1), .in2(1'b1), .in3(1'b1), .in4(1'b1), .in5(1'b1), .in6(1'b1), .in7(1'b1),
    .in8(1'b1), .in9(1'b1), .in10(1'b1), .in11(1'b1), .in12(1'b1), .in13(1'b1), .in14(1'b1), .in15(1'b1),
    .out(multiplexer_4_out), .sel(subtractor_1_out));
endmodule

module BranchControl (
  input  OP1,
  input  OP2,
  input  OP3,
  input  OP4,
  output BranchEqual,
  output BrancNotEqual
);

  wire not_1_out, not_2_out, not_3_out, not_4_out, not_5_out;

  not not_1 (not_1_out, OP2);
  not not_2 (not_2_out, OP3);
  not not_3 (not_3_out, OP2);
  not not_4 (not_4_out, OP3);
  not not_5 (not_5_out, OP4);
  and and_1 (BranchEqual, OP1, not_1_out, not_2_out, OP4);
  and and_2 (BrancNotEqual, OP1, not_3_out, not_4_out, not_5_out);
endmodule

module SignalControl (
  input  OP1,
  input  OP2,
  input  OP3,
  input  OP4,
  input  FUNCT,
  output ALUSRC,
  output ALUOP1,
  output ALUOP2,
  output RegWrite,
  output J,
  output JR,
  output JAL,
  output MemRead,
  output MemWrite,
  output MemToReg,
  output PUT,
  output HALT
);

  wire and_3_out, and_4_out, and_6_out, and_7_out, and_8_out, and_9_out, not_1_out, not_2_out, not_3_out,
       not_4_out, not_5_out, not_6_out, not_7_out, not_8_out, not_9_out, not_10_out, not_11_out, not_12_out,
       not_13_out, not_14_out, not_15_out, not_16_out, not_17_out, not_18_out, not_19_out, not_20_out,
       not_21_out, not_22_out, not_23_out, not_24_out, not_25_out, not_26_out, not_27_out, not_28_out,
       not_29_out, not_30_out;

  not not_1 (not_1_out, OP2);
  not not_2 (not_2_out, OP3);
  not not_3 (not_3_out, OP1);
  not not_4 (not_4_out, OP3);
  not not_5 (not_5_out, OP4);
  not not_6 (not_6_out, OP1);
  not not_7 (not_7_out, OP1);
  not not_8 (not_8_out, OP1);
  not not_9 (not_9_out, OP2);
  not not_10 (not_10_out, OP1);
  not not_11 (not_11_out, OP2);
  not not_12 (not_12_out, OP1);
  not not_13 (not_13_out, FUNCT);
  not not_14 (not_14_out, OP1);
  not not_15 (not_15_out, OP3);
  not not_16 (not_16_out, OP4);
  not not_17 (not_17_out, OP3);
  not not_18 (not_18_out, OP4);
  not not_19 (not_19_out, OP2);
  not not_20 (not_20_out, OP4);
  not not_21 (not_21_out, OP2);
  not not_22 (not_22_out, OP1);
  not not_23 (not_23_out, FUNCT);
  not not_24 (not_24_out, OP1);
  not not_25 (not_25_out, OP1);
  not not_26 (not_26_out, FUNCT);
  not not_27 (not_27_out, OP1);
  not not_28 (not_28_out, OP2);
  not not_29 (not_29_out, OP3);
  not not_30 (not_30_out, OP4);
  and and_1 (HALT, OP1, OP2, OP3, OP4);
  and and_2 (ALUSRC, OP1, not_1_out, not_2_out);
  and and_3 (and_3_out, not_3_out, OP2, not_4_out, not_5_out);
  and and_4 (and_4_out, not_6_out, OP2, OP3, OP4);
  and and_5 (ALUOP2, not_7_out, OP3, OP4);
  and and_6 (and_6_out, not_8_out, not_9_out, OP4);
  and and_7 (and_7_out, not_10_out, not_11_out, OP3);
  and and_8 (and_8_out, not_12_out, OP3, OP4, not_13_out);
  and and_9 (and_9_out, not_14_out, OP2, not_15_out, not_16_out);
  and and_10 (J, OP1, OP2, not_17_out, not_18_out);
  and and_11 (JR, OP1, not_19_out, OP3, not_20_out);
  and and_12 (JAL, OP1, not_21_out, OP3, OP4);
  and and_13 (MemRead, not_22_out, OP2, OP3, OP4, not_23_out);
  and and_14 (MemWrite, not_24_out, OP2, OP3, OP4, FUNCT);
  and and_15 (MemToReg, not_25_out, OP2, OP3, OP4, not_26_out);
  and and_16 (PUT, not_27_out, not_28_out, not_29_out, not_30_out);
  or or_1 (ALUOP1, and_3_out, and_4_out);
  or or_2 (RegWrite, and_6_out, and_7_out, and_8_out, and_9_out);
endmodule
